// Logisim project Processor_8.circ as structural Verilog
module Latches (
  input  D,
  input  S,
  input  E,
  input  E_2,
  input  R,
  input  D_2,
  input  E_3,
  output Q,
  output Q_2,
  output Q_bar,
  output Q_3,
  output Q_bar_2
);

  wire nand_1_out, nand_2_out, nand_3_out, nand_4_out, nand_9_out, nand_10_out, nand_12_out, not_1_out;

  not not_1 (not_1_out, D_2);
  nand nand_1 (nand_1_out, S, E);
  nand nand_2 (nand_2_out, E, R);
  nand nand_3 (nand_3_out, D_2, E_3);
  nand nand_4 (nand_4_out, E_3, not_1_out);
  nand nand_5 (Q_2, nand_1_out, Q_bar);
  nand nand_6 (Q_bar, Q_2, nand_2_out);
  nand nand_7 (Q_3, nand_3_out, Q_bar_2);
  nand nand_8 (Q_bar_2, Q_3, nand_4_out);
  nand nand_9 (nand_9_out, D, E_2);
  nand nand_10 (nand_10_out, nand_9_out, E_2);
  nand nand_11 (Q, nand_9_out, nand_12_out);
  nand nand_12 (nand_12_out, Q, nand_10_out);

  // Notes on the sheet:
  //   SR
  //   D-FlipFlop 
  //   1-Bit-Memory Cell
endmodule

module P_MEM1 (
  input  D,
  input  E,
  output Q
);

  wire nand_1_out, nand_2_out, nand_4_out;

  nand nand_1 (nand_1_out, D, E);
  nand nand_2 (nand_2_out, nand_1_out, E);
  nand nand_3 (Q, nand_1_out, nand_4_out);
  nand nand_4 (nand_4_out, Q, nand_2_out);

  // Notes on the sheet:
  //   1-Bit-Memory Cell
endmodule

module P_MEM8 (
  input  [7:0] in_1,
  input  in_2,
  output [7:0] out_3
);

  P_MEM1 p_mem1_1 (.D(in_1[0]), .E(in_2), .Q(out_3[0]));
  P_MEM1 p_mem1_2 (.D(in_1[1]), .E(in_2), .Q(out_3[1]));
  P_MEM1 p_mem1_3 (.D(in_1[2]), .E(in_2), .Q(out_3[2]));
  P_MEM1 p_mem1_4 (.D(in_1[3]), .E(in_2), .Q(out_3[3]));
  P_MEM1 p_mem1_5 (.D(in_1[4]), .E(in_2), .Q(out_3[4]));
  P_MEM1 p_mem1_6 (.D(in_1[5]), .E(in_2), .Q(out_3[5]));
  P_MEM1 p_mem1_7 (.D(in_1[6]), .E(in_2), .Q(out_3[6]));
  P_MEM1 p_mem1_8 (.D(in_1[7]), .E(in_2), .Q(out_3[7]));
endmodule

module P_ENABLE (
  input  [7:0] in_1,
  input  in_2,
  output [7:0] out_3
);

  and and_1 (out_3[0], in_1[0], in_2);
  and and_2 (out_3[1], in_1[1], in_2);
  and and_3 (out_3[2], in_1[2], in_2);
  and and_4 (out_3[3], in_1[3], in_2);
  and and_5 (out_3[4], in_1[4], in_2);
  and and_6 (out_3[5], in_1[5], in_2);
  and and_7 (out_3[6], in_1[6], in_2);
  and and_8 (out_3[7], in_1[7], in_2);
endmodule

module P_REG_8 (
  input  [7:0] in_1,
  input  E1,
  input  E2,
  output [7:0] out_4
);

  wire [7:0] p_mem8_1_out_3;

  P_MEM8 p_mem8_1 (.in_1(in_1), .out_3(p_mem8_1_out_3), .in_2(E1));
  P_ENABLE p_enable_1 (.in_1(p_mem8_1_out_3), .out_3(out_4), .in_2(E2));
endmodule
